// Logisim project 1.circ as structural Verilog: 1 circuit, main circuit main
module main (
  input  A,
  input  in_2,
  input  in_3,
  input  D,
  input  E,
  output out_6
);

  wire nand_1_out, nand_2_out, nand_3_out, nand_4_out, nand_5_out, nand_6_out, nand_7_out, nand_8_out,
       nand_9_out, nand_10_out, nand_11_out;

  nand nand_1 (nand_1_out, A, A);
  nand nand_2 (nand_2_out, in_2, in_2);
  nand nand_3 (nand_3_out, in_3, in_3);
  nand nand_4 (nand_4_out, D, D);
  nand nand_5 (nand_5_out, E, E);
  nand nand_6 (nand_6_out, nand_1_out, nand_1_out);
  nand nand_7 (nand_7_out, nand_2_out, nand_2_out);
  nand nand_8 (nand_8_out, nand_5_out, nand_5_out);
  nand nand_9 (nand_9_out, nand_2_out, nand_4_out);
  nand nand_10 (nand_10_out, nand_7_out, nand_8_out);
  nand nand_11 (nand_11_out, nand_6_out, nand_7_out, nand_3_out);
  nand nand_12 (out_6, nand_11_out, nand_9_out, nand_10_out);

  // Notes on the sheet:
  //   B
  //   C
endmodule
