// Logisim project 2.circ as structural Verilog: 1 circuit, main circuit main
module main (
  input  A,
  input  B,
  input  C,
  input  A_2,
  input  B_2,
  input  C_2,
  output out_7,
  output out_8
);

  wire not_1_out, not_2_out, not_3_out, or_1_out;

  not not_1 (not_1_out, A_2);
  not not_2 (not_2_out, B_2);
  not not_3 (not_3_out, C_2);
  or or_1 (or_1_out, A, B, C);
  not not_4 (out_7, or_1_out);
  and and_1 (out_8, not_1_out, not_2_out, not_3_out);
endmodule
