// Logisim project 2BIT.circ as structural Verilog: 1 circuit, main circuit main
module main (
  input  A1,
  input  AO,
  input  B1,
  input  B0,
  output A_B,
  output A_B_2,
  output A_B_3
);

  wire and_1_out, and_2_out, and_3_out, and_4_out, and_5_out, and_6_out, not_1_out, not_2_out, not_3_out,
       not_4_out, not_5_out, not_6_out, not_7_out, not_8_out, xnor_1_out, xnor_2_out;

  not not_1 (not_1_out, B0);
  not not_2 (not_2_out, B0);
  not not_3 (not_3_out, B1);
  not not_4 (not_4_out, B1);
  not not_5 (not_5_out, AO);
  not not_6 (not_6_out, A1);
  not not_7 (not_7_out, AO);
  not not_8 (not_8_out, A1);
  xnor xnor_1 (xnor_1_out, AO, B0);
  xnor xnor_2 (xnor_2_out, A1, B1);
  and and_1 (and_1_out, AO, not_2_out, not_3_out);
  and and_2 (and_2_out, A1, not_4_out);
  and and_3 (and_3_out, not_5_out, B0, not_6_out);
  and and_4 (and_4_out, not_7_out, B0, B1);
  and and_5 (and_5_out, AO, not_1_out, A1);
  and and_6 (and_6_out, not_8_out, B1);
  and and_7 (A_B, xnor_1_out, xnor_2_out);
  or or_1 (A_B_2, and_5_out, and_1_out, and_2_out);
  or or_2 (A_B_3, and_3_out, and_4_out, and_6_out);
endmodule
